# Fritzing sketch valve-controller (saved by Fritzing 0.9.10b)
circuit board: 7.36892cm x 5.10543cm
perfboards: 1

parts:
  J1 = female pin header, 15 pins [form="♀ (female)"]
  L1 = LED - 5mm [color="Orange (620nm)" current=0.030 package="5 mm [THT]"]
  L2 = LED - 5mm [color="Orange (620nm)" current=0.030 package="5 mm [THT]"]
  L3 = LED - 5mm [color="Orange (620nm)" current=30mA package="5 mm [THT]"]
  L4 = LED - 5mm [color="Orange (620nm)" current=0.030 package="5 mm [THT]"]
  L5 = LED - 5mm [color="Orange (620nm)" current=0.030 package="5 mm [THT]"]
  R2 = Resistor [tolerance=±5% power=0.25 resistance=220 package=THT]
  R4 = Resistor [tolerance=±5% power=0.25 resistance=220 package=THT]
  R5 = Resistor [tolerance=±5% power=0.25 resistance=220 package=THT]
  Q1 = Basic FET N-Channel [package="TO220 [THT]"]
  Q2 = Basic FET N-Channel [package="TO220 [THT]"]
  Q4 = Basic FET N-Channel [package="TO220 [THT]"]
  Q5 = Basic FET N-Channel [package="TO220 [THT]"]
  J3 = Camdenboss CTB0158-2 [part_number=CTB0158-2 package=THT]
  R3 = Resistor [tolerance=±5% power=0.25 resistance=220 package=THT]
  R1 = Resistor [tolerance=±5% power=0.25 resistance=220 package=THT]
  J5 = Camdenboss CTB0158-3 [part_number=CTB0158-3 package=THT]
  J4 = Camdenboss CTB0158-2 [part_number=CTB0158-2 package=THT]
  J2 = female pin header, 15 pins [form="♀ (female)"]
  Q3 = Basic FET N-Channel [package="TO220 [THT]"]
  Arduino_Nano = Arduino Nano (Rev3.0)

nets:
  N1: J1.pin1, Arduino_Nano.D13/SCK
  N2: J1.pin2, Arduino_Nano.3V3
  N3: J1.pin3, Arduino_Nano.AREF
  N4: J1.pin4, Arduino_Nano.A0
  N5: J1.pin5, Arduino_Nano.A1
  N6: J1.pin6, Arduino_Nano.A2
  N7: J1.pin7, Arduino_Nano.A3
  N8: J1.pin8, Arduino_Nano.A4
  N9: J1.pin9, Arduino_Nano.A5
  N10: J1.pin10, Arduino_Nano.A6
  N11: J1.pin11, Arduino_Nano.A7
  N12: J1.pin12, Arduino_Nano.5V
  N13: J1.pin13, J2.pin13, Arduino_Nano.RESET
  N14: J1.pin14, L1.cathode, L2.cathode, L3.cathode, L4.cathode, L5.cathode, Q1.source, Q2.source, Q4.source, Q5.source, J3.pin2, J2.pin12, Q3.source, Arduino_Nano.GND
  N15: J1.pin15, J3.pin1, Arduino_Nano.VIN
  N16: L1.anode, R1.Pin_1
  N17: L2.anode, R2.Pin_0
  N18: L3.anode, R3.Pin_0
  N19: L4.anode, R4.Pin_1
  N20: L5.anode, R5.Pin_1
  N21: R2.Pin_1, Q2.gate, J2.pin10, Arduino_Nano.D3
  N22: R4.Pin_0, Q4.gate, J2.pin8, Arduino_Nano.D5
  N23: R5.Pin_0, Q5.gate, J2.pin7, Arduino_Nano.D6
  N24: Q1.gate, R1.Pin_0, J2.pin11, Arduino_Nano.D2
  N25: Q1.drain, J4.pin1
  N26: Q2.drain, J4.pin2
  N27: Q4.drain, J5.pin2
  N28: Q5.drain, J5.pin3
  N29: R3.Pin_1, J2.pin9, Q3.gate, Arduino_Nano.D4
  N30: J5.pin1, Q3.drain
  N31: J2.pin1, Arduino_Nano.D12/MISO
  N32: J2.pin2, Arduino_Nano.D11/MOSI
  N33: J2.pin3, Arduino_Nano.D10
  N34: J2.pin4, Arduino_Nano.D9
  N35: J2.pin5, Arduino_Nano.D8
  N36: J2.pin6, Arduino_Nano.D7
  N37: J2.pin14, Arduino_Nano.D0/RX
  N38: J2.pin15, Arduino_Nano.D1/TX

notes:
  +12V
  GND
  VSAA1
  VSAA2
  VSAA3
  VSAA4
  VSAA5
